# Fritzing sketch Schematic Gyroscope (saved by Fritzing 1.0.7)
breadboards: 1

parts:
  Raspberry_Pi_Pico = Raspberry Pi Pico or Pico 2
  Part1 = InvenSense MPU6050
  Q1 = NPN-Transistor [part_number=2n222 package="TO92 [THT]"]
  R1 = Resistor [tolerance=±5% power=0.25W resistance=220 package=THT]
  SP1 = SPEAKER [package=pcb_mount_speaker]

nets:
  N1: Raspberry_Pi_Pico.pin_7, R1.Pin_1
  N2: Raspberry_Pi_Pico.pin_8, Raspberry_Pi_Pico.pin_18, Raspberry_Pi_Pico.pin_23, Raspberry_Pi_Pico.pin_38, Part1.GND, Q1.E
  N3: Raspberry_Pi_Pico.pin_21, Part1.SDA
  N4: Raspberry_Pi_Pico.pin_22, Part1.SCL
  N5: Raspberry_Pi_Pico.pin_36, Part1.VCC
  N6: Raspberry_Pi_Pico.pin_40, SP1.-
  N7: Q1.B, R1.Pin_0
  N8: Q1.C, SP1.+

custom parts:
  Raspberry Pi Pico or Pico 2: Raspberry Pi Pico and Pico 2. Based around the RP2040 and RP2350 microcontrollers respectively, Picos are low cost microcontroller device bringing Raspberry Pi quality, cost, and easy of use to the microcontroller space. Jan 2021, Split part in to two versions: tht (this one) and SMD. This one will drill holes for a .1 in header in pcb to allow plugging in the module as well as providing pads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
