# Fritzing sketch Schematic Tetris (saved by Fritzing 1.0.7)
breadboards: 1

parts:
  Pico/Pico2_Mod_1 = Raspberry Pi Pico or Pico 2
  Mod1 = Passive Buzzer
  Display1 = 4-Digit 7-segment LED Display [package=THT]
  Part2 = Black Joystick KY-023
  Part3 = 4x Matrix LED 8x8 with MAX7219 [part_number=FC-16]

nets (from the breadboard view):
  N1: Pico/Pico2_Mod_1.pin_1, Mod1.S
  GND: Pico/Pico2_Mod_1.pin_3, Pico/Pico2_Mod_1.pin_8, Pico/Pico2_Mod_1.pin_13, Pico/Pico2_Mod_1.pin_18, Pico/Pico2_Mod_1.pin_23, Pico/Pico2_Mod_1.pin_28, Pico/Pico2_Mod_1.pin_33, Pico/Pico2_Mod_1.pin_38, Pico/Pico2_Mod_1.pin_42, Mod1.-, Display1.GND, Part2.GND, Part3.GND#1
  N2: Pico/Pico2_Mod_1.pin_4, Display1.CLK
  N3: Pico/Pico2_Mod_1.pin_5, Display1.DIO
  N4: Pico/Pico2_Mod_1.pin_15, Part3.DIN
  N5: Pico/Pico2_Mod_1.pin_17, Part3.CS
  N6: Pico/Pico2_Mod_1.pin_19, Part3.CLK
  N7: Pico/Pico2_Mod_1.pin_29, Part2.SW
  N8: Pico/Pico2_Mod_1.pin_31, Part2.VRy
  N9: Pico/Pico2_Mod_1.pin_32, Part2.VRx
  N10: Pico/Pico2_Mod_1.pin_36, Display1.VCC
  +5V: Pico/Pico2_Mod_1.pin_39, Mod1.NC, Part2.+5V, Part3.VCC

custom parts:
  Raspberry Pi Pico or Pico 2: Raspberry Pi Pico and Pico 2. Based around the RP2040 and RP2350 microcontrollers respectively, Picos are low cost microcontroller device bringing Raspberry Pi quality, cost, and easy of use to the microcontroller space. Jan 2021, Split part in to two versions: tht (this one) and SMD. This one will drill holes for a .1 in header in pcb to allow plugging in the module as well as providing pads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
  4-Digit 7-segment LED Display: A 4-digit 7-segments LED display PCB module driven by a TM1637 control IC via 1-wire protocol.
  Black Joystick KY-023: Description: The joystick is a combination of 2 analoog potentiometer and a digital switch. Arduino GND --> Module pin - Arduino +5V --> Module pin +5V Arduino Analoog 0 --> Module VRx Arduino Analoog 1 --> Module VRy Arduino Digital --> Module SW Dimensions: 1" x 1.25"
  4x Matrix LED 8x8 with MAX7219: FC-16
