# Fritzing sketch Schematic Radar (saved by Fritzing 1.0.7)
breadboards: 1

parts:
  Pico/Pico2_Mod_1 = Raspberry Pi Pico or Pico 2
  Mod1 = Passive Buzzer
  R1 = Resistor [tolerance=±5% power=0.25W resistance=1000 package=THT]
  R2 = Resistor [tolerance=±5% power=0.25W resistance=1000 package=THT]  # not connected
  M2 = Dagu DGServo 9g (Top view) [part_number=RS001B]
  HC-SR04_Sensor_1 = HC-SR04 Ultrasonic Distance Sensor
  R3 = Resistor [tolerance=±5% power=0.25W resistance=1k package=THT]

nets (from the schematic view):
  GND: Pico/Pico2_Mod_1.pin_3, Pico/Pico2_Mod_1.pin_13, Pico/Pico2_Mod_1.pin_18, Pico/Pico2_Mod_1.pin_23, Pico/Pico2_Mod_1.pin_28, Pico/Pico2_Mod_1.pin_33, Pico/Pico2_Mod_1.pin_38, Pico/Pico2_Mod_1.pin_42, Mod1.-, M2.gnd, HC-SR04_Sensor_1.GND, R3.Pin_1
  N1: Pico/Pico2_Mod_1.pin_19, R1.Pin_0, R3.Pin_0
  N2: Pico/Pico2_Mod_1.pin_24, Mod1.S
  N3: Pico/Pico2_Mod_1.pin_25, HC-SR04_Sensor_1.TRIG
  N4: Pico/Pico2_Mod_1.pin_34, M2.pulse
  VCC: Pico/Pico2_Mod_1.pin_40, Mod1.NC, M2.vcc, HC-SR04_Sensor_1.VCC
  N5: R1.Pin_1, HC-SR04_Sensor_1.ECHO

custom parts:
  Raspberry Pi Pico or Pico 2: Raspberry Pi Pico and Pico 2. Based around the RP2040 and RP2350 microcontrollers respectively, Picos are low cost microcontroller device bringing Raspberry Pi quality, cost, and easy of use to the microcontroller space. Jan 2021, Split part in to two versions: tht (this one) and SMD. This one will drill holes for a .1 in header in pcb to allow plugging in the module as well as providing pads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
